// Logisim project trabalho sd.circ as structural Verilog
// agua
module modulo_de_agua (
  input  BI,
  input  SNA,
  input  STA,
  output VA,
  output RAQ,
  output FCA
);

  wire and_1_out, and_2_out, and_3_out, and_4_out, clock_1_out, or_1_out, or_2_out, T0_q, T0_qn, T1_q, T1_qn;

  and and_1 (and_1_out, SNA, T0_q);
  and and_2 (and_2_out, T0_q, T1_q);
  and and_3 (and_3_out, STA, T1_q);
  and and_4 (and_4_out, T0_qn, BI, T1_qn);
  or or_1 (or_1_out, and_1_out, and_2_out);
  or or_2 (or_2_out, and_1_out, and_2_out, and_3_out, and_4_out);
  Clock clock_1 (.out(clock_1_out));
  T_Flip_Flop T1 (.clk(clock_1_out), .T(or_1_out), .Q(T1_q), .Qn(T1_qn));  // open: preset, reset, en
  T_Flip_Flop T0 (.clk(clock_1_out), .T(or_2_out), .Q(T0_q), .Qn(T0_qn));  // open: preset, reset, en
  and and_5 (VA, T0_q, T1_qn);
  and and_6 (RAQ, T1_q, T0_qn);
  and and_7 (FCA, T0_q, T1_q);
endmodule

// lavagem
module modulo_de_lavagem (
  input  FCA,
  input  SNA,
  output MD_1,
  output MD_2,
  output ME_1,
  output ME_2,
  output BA,
  output MC,
  output FCL
);

  wire and_1_out, and_2_out, and_3_out, and_4_out, clock_1_out, not_1_out, or_1_out, or_2_out, T0_q, T0_qn,
       T1_q, T1_qn, T2_q, T2_qn, xor_1_out;

  not not_1 (not_1_out, SNA);
  and and_1 (and_1_out, T0_q, T1_q);
  and and_2 (and_2_out, T0_q, T2_qn);
  and and_3 (and_3_out, T0_q, not_1_out);
  xor xor_1 (xor_1_out, T0_q, T2_q);
  and and_4 (and_4_out, FCA, T0_qn, T1_qn);
  Clock clock_1 (.out(clock_1_out));
  or or_1 (or_1_out, and_2_out, and_1_out, and_3_out);
  or or_2 (or_2_out, T1_q, and_3_out, xor_1_out, and_4_out);
  T_Flip_Flop T2 (.clk(clock_1_out), .T(and_1_out), .Q(T2_q), .Qn(T2_qn));  // open: preset, reset, en
  T_Flip_Flop T1 (.clk(clock_1_out), .T(or_1_out), .Q(T1_q), .Qn(T1_qn));  // open: preset, reset, en
  T_Flip_Flop T0 (.clk(clock_1_out), .T(or_2_out), .Q(T0_q), .Qn(T0_qn));  // open: preset, reset, en
  and and_5 (MD_1, T1_qn, T0_q, T2_qn);
  and and_6 (MD_2, T1_q, T0_qn, T2_qn);
  and and_7 (ME_1, T2_qn, T1_q, T0_q);
  and and_8 (ME_2, T2_q, T0_qn, T1_qn);
  and and_9 (BA, T2_q, T1_qn, T0_q);
  and and_10 (MC, T1_q, T2_q, T0_qn);
  and and_11 (FCL, T0_q, T1_q, T2_q);
endmodule

module modulode_controlo_da_maquina (
  input  BI,
  input  SNA,
  input  STA,
  output ACA,
  output ACL
);

  wire and_1_out, and_2_out, and_3_out, clock_1_out, modulo_de_agua_1_fca, modulo_de_lavagem_1_fcl, or_1_out,
       or_2_out, T0_qn, T1_qn;

  modulo_de_agua modulo_de_agua_1 (.BI(BI), .SNA(SNA), .STA(STA), .FCA(modulo_de_agua_1_fca));  // open: VA, RAQ
  and and_1 (and_1_out, BI, T0_qn, T1_qn);
  modulo_de_lavagem modulo_de_lavagem_1 (
    .FCA(modulo_de_agua_1_fca), .SNA(SNA), .FCL(modulo_de_lavagem_1_fcl));  // open: MD_1, MD_2, ME_1, ME_2, BA, MC
  and and_2 (and_2_out, modulo_de_lavagem_1_fcl, ACL);
  and and_3 (and_3_out, modulo_de_agua_1_fca, ACA);
  Clock clock_1 (.out(clock_1_out));
  or or_1 (or_1_out, and_2_out, and_3_out);
  or or_2 (or_2_out, and_3_out, and_1_out);
  T_Flip_Flop T1 (.clk(clock_1_out), .T(or_1_out), .Q(ACL), .Qn(T1_qn));  // open: preset, reset, en
  T_Flip_Flop T0 (.clk(clock_1_out), .T(or_2_out), .Q(ACA), .Qn(T0_qn));  // open: preset, reset, en
endmodule
